# Fritzing sketch KetosensePi_0.1 (saved by Fritzing 0.9.3b)
breadboards: 1

parts:
  TGS822 = Gas Sensor Breakout Board
  I2C_LCD1 = I2C LCD screen
  IC1 = DIP - 14 pins [chip_label=MCP3204-C package="DIP (Dual Inline) [THT]"]
  R1 = Resistor [tolerance=±5% resistance=1k package=THT]
  RHT1 = Humidity and Temperature Sensor RHT03
  S1 = Pushbutton [package="[THT]"]
  R2 = Resistor [tolerance=±5% resistance=10k package=THT]
  S2 = Pushbutton [package="[THT]"]
  S3 = Pushbutton [package="[THT]"]
  R3 = Resistor [tolerance=±5% resistance=10k package=THT]
  R4 = Resistor [tolerance=±5% resistance=10k package=THT]
  Part2 = Adafruit T-Cobbler Plus [part_number="Adafruit #1989 and #2028"]
  R5 = Resistor [tolerance=±5% resistance=10k package=THT]
  R6 = Resistor [tolerance=±5% resistance=10k package=THT]
  R7 = Resistor [tolerance=±5% resistance=10k package=THT]

nets (from the breadboard view):
  N1: TGS822.A1, R1.Pin_0, R5.Pin_1
  VCC: TGS822.B1, TGS822.H1, I2C_LCD1.VCC, Part2.+5V
  GND: TGS822.GND, I2C_LCD1.GND, IC1.DGND, IC1.AGND, R1.Pin_1, RHT1.GND_2, R2.Pin_1, R3.Pin_1, R4.Pin_1, Part2.GND, R7.Pin_0
  N2: I2C_LCD1.SDA, Part2.SDA
  N3: I2C_LCD1.SCL, Part2.SCL
  N4: IC1.CH0, R5.Pin_0, R6.Pin_1
  N5: IC1.CS/SHDN, Part2.CE1
  N6: IC1.D_IN, Part2.MOSI
  N7: IC1.D_OUT, Part2.MISO
  N8: IC1.CLK, Part2.SCLK
  N9: IC1.V_REF, IC1.V_DD, RHT1.Vcc, S1.Pin_3, S1.Pin_4, S2.Pin_3, S2.Pin_4, S3.Pin_3, S3.Pin_4, Part2.+3.3V_2
  N10: RHT1.Data-signal, Part2.GPIO12
  N11: S1.Pin_1, S1.Pin_2, R2.Pin_0, Part2.GPIO5
  N12: S2.Pin_1, S2.Pin_2, R3.Pin_0, Part2.GPIO6
  N13: S3.Pin_1, S3.Pin_2, R4.Pin_0, Part2.GPIO13
  N14: R6.Pin_0, R7.Pin_1

notes:
  KetoSense for RasPi 2/3
  The KetoSense is a prototype breath analyzer to detect ethanol in the breath, a proxy for ketogenesis.
  This configuration uses the TGS 822 gas sensor, Raspberry Pi 2, and various parts from the Osoyoo Raspberry Pi Starter Kit.
  Changed from 10k to 1k
  Additional voltage divider to step down from 5V to 3.3V
  DHT11 with PCB 3-pin output. Uses 3.3V input/output
  LCD with I2C bus PCB. 4-pin connection uses 5V input, provides I2C outputs at 3.3V.

custom parts:
  I2C LCD screen: An I2C-based 2x16 character display included in Osoyoo Raspberry Pi kits.
  DIP - 14 pins: A DIP stand-in part for whatever IC you want. With 14 pins on a 300mil dual inline package (DIP) footprint.
  Adafruit T-Cobbler Plus: The Raspberry Pi has landed on the Maker World like a 40-GPIO pinned, quad-USB ported, credit card sized bomb of DIY joy. And while you can use most of our great Model B accessories by hooking up our downgrade cable, its probably a good time to upgrade your set up and accessorize using all of the 40 pins. That's why we now carry the Assembled Adafruit Pi T-Cobbler Plus - Breakout + Cable for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
